# Fritzing sketch 555timerwithspeakerfritzing (saved by Fritzing 0.9.3b)
breadboards: 1

parts:
  U1 = 555 Timer [package="SO8 [SMD]"]  # not connected
  VCC1 = Battery block 9V
  SP1 = SPEAKER [package=pcb_mount_speaker]
  C1 = Electrolytic Capacitor [capacitance=1µF package="100 mil [THT, electrolytic]"]
  C2 = Electrolytic Capacitor [capacitance=1µF package="100 mil [THT, electrolytic]"]
  R1 = Resistor [tolerance=±5% resistance=220 package=THT]
  R2 = Resistor [tolerance=±5% resistance=220 package=THT]

nets:
  N1: VCC1.-, SP1.+, C2.-
  N2: VCC1.+, R1.Pin_0
  N3: SP1.-, C1.-
  N4: C2.+, R2.Pin_1
  N5: R1.Pin_1, R2.Pin_0
