# Fritzing sketch PiezoSensordenElektrikÜretimiFritzing (saved by Fritzing 0.9.3b)
breadboards: 1

parts:
  D1 = Rectifier Diode [part_number=1N4001 package="300 mil [THT]"]
  D2 = Rectifier Diode [part_number=1N4001 package="300 mil [THT]"]
  D3 = Rectifier Diode [part_number=1N4001 package="300 mil [THT]"]
  D4 = Rectifier Diode [part_number=1N4001 package="300 mil [THT]"]
  C1 = Electrolytic Capacitor [capacitance=10µF voltage=10V package="100 mil [THT, electrolytic]"]
  LED1 = LED - 5mm [color="White (4500K)" package="5 mm [THT]"]
  Piezoelectric_Sensor1 = Piezoelectric Sensor

nets:
  N1: D1.cathode, D3.anode, Piezoelectric_Sensor1.GND
  N2: D1.anode, D2.anode, C1.-, LED1.cathode
  N3: D2.cathode, D4.anode, Piezoelectric_Sensor1.VCC
  N4: D3.cathode, D4.cathode, C1.+, LED1.anode

notes:
  Piezo Sensörü videonun altındaki linkten indirebilirsiniz.

custom parts:
  Piezoelectric Sensor: Piezoelectric sensor.
