# Fritzing sketch lm7805frıtzıng (saved by Fritzing 0.9.3b)
breadboards: 1

parts:
  IC1 = Voltage Regulator [package=78xxl]
  BAT1 = BC9VPC [package=bc9vpc]
  C1 = Electrolytic Capacitor [capacitance=1µF package="100 mil [THT, electrolytic]"]
  C2 = Electrolytic Capacitor [capacitance=1µF package="100 mil [THT, electrolytic]"]
  R1 = Resistor [tolerance=±5% resistance=220 package=THT]
  LED1 = LED - 5mm [color="Red (633nm)" package="5 mm [THT]"]

nets:
  N1: IC1.GND, BAT1.V-, LED1.cathode
  N2: IC1.IN, C1.+
  N3: IC1.OUT, C2.+, R1.Pin_0
  N4: BAT1.V+, C1.-, C2.-
  N5: R1.Pin_1, LED1.anode
